// Logisim project clock_divider.circ as structural Verilog: 1 circuit, main circuit main
// Clock divider
module main (
  output out_1
);

  wire AND_out, button_1_out, clock_2_out, Clock_out, counter_1_carry, d_ff_1_q, d_ff_2_q, XOR_out;
  wire [1:0] counter_1_q;

  Button button_1 (.out(button_1_out));
  Clock Clock (.out(Clock_out));
  // Probe on counter_1_q
  Counter #(.width(2), .max('h2)) counter_1 (
    .load(button_1_out), .D(2'b00), .count(1'b1), .Q(counter_1_q), .carry(counter_1_carry), .clk(Clock_out));  // open: clr
  // Probe on counter_1_carry
  xor XOR (XOR_out, counter_1_carry, d_ff_1_q);
  Clock clock_2 (.out(clock_2_out));
  D_Flip_Flop d_ff_1 (.clk(clock_2_out), .D(XOR_out), .Q(d_ff_1_q));  // open: Qn, preset, en, reset
  D_Flip_Flop d_ff_2 (.clk(clock_2_out), .D(d_ff_1_q), .Q(d_ff_2_q));  // open: Qn, preset, en, reset
  and AND (AND_out, d_ff_1_q, ~d_ff_2_q);  // AND_Gate
  // Probe on AND_out

  // Notes on the sheet:
  //   Corner
endmodule
