// Logisim project digit_display.circ as structural Verilog: 1 circuit, main circuit main
module main (
);

  wire and_1_out, and_2_out, and_3_out, and_4_out, and_5_out, and_6_out, and_7_out, and_8_out, and_9_out,
       and_10_out, and_11_out, clock_1_out, clock_2_out, clock_3_out, clock_4_out, clock_5_out, clock_6_out,
       clock_7_out, d_ff_1_q, d_ff_2_q, d_ff_3_q, d_ff_4_q, d_ff_5_q, d_ff_6_q, d_ff_7_q, d_ff_12_q,
       d_ff_13_q, d_ff_14_q, d_ff_15_q, or_1_out, or_2_out, or_3_out, or_4_out, or_5_out;
  wire [1:0] rom_1_data;
  wire [3:0] d_ff_8_q;
  wire [4:0] counter_1_q;
  wire [6:0] rom_2_data;

  Clock clock_1 (.out(clock_1_out));
  Counter #(.width(5), .max('h1f)) counter_1 (
    .load(1'b0), .D({5{1'b0}}), .count(1'b1), .Q(counter_1_q), .clk(clock_1_out), .clr(1'b0));  // open: carry
  ROM #(.addrWidth(5), .dataWidth(2)) rom_1 (.addr(counter_1_q), .data(rom_1_data));  // open: sel
  Clock clock_2 (.out(clock_2_out));
  or or_1 (or_1_out, and_2_out, rom_1_data[0]);
  Clock clock_3 (.out(clock_3_out));
  or or_2 (or_2_out, and_3_out, and_7_out);
  Clock clock_4 (.out(clock_4_out));
  or or_3 (or_3_out, and_4_out, and_8_out);
  Clock clock_5 (.out(clock_5_out));
  or or_4 (or_4_out, and_5_out, and_9_out);
  Clock clock_6 (.out(clock_6_out));
  or or_5 (or_5_out, 1'b0, and_10_out);
  Clock clock_7 (.out(clock_7_out));
  and and_1 (and_1_out, ~rom_1_data[1], 1'b1);  // AND_Gate
  and and_2 (and_2_out, ~and_3_out, d_ff_8_q[0]);  // AND_Gate
  D_Flip_Flop d_ff_1 (.clk(clock_2_out), .D(or_1_out), .Q(d_ff_1_q));  // open: Qn, preset, en, reset
  and and_3 (and_3_out, ~and_4_out, d_ff_8_q[1]);  // AND_Gate
  D_Flip_Flop d_ff_2 (.clk(clock_3_out), .D(or_2_out), .Q(d_ff_2_q));  // open: Qn, preset, en, reset
  and and_4 (and_4_out, ~and_5_out, d_ff_8_q[2]);  // AND_Gate
  D_Flip_Flop d_ff_3 (.clk(clock_4_out), .D(or_3_out), .Q(d_ff_3_q));  // open: Qn, preset, en, reset
  and and_5 (and_5_out, ~and_6_out, d_ff_8_q[3]);  // AND_Gate
  D_Flip_Flop d_ff_4 (.clk(clock_5_out), .D(or_4_out), .Q(d_ff_4_q));  // open: Qn, preset, en, reset
  and and_6 (and_6_out, ~1'b0, d_ff_12_q);  // AND_Gate
  D_Flip_Flop d_ff_5 (.clk(clock_6_out), .D(or_5_out), .Q(d_ff_5_q));  // open: Qn, preset, en, reset
  D_Flip_Flop d_ff_6 (.clk(clock_7_out), .D(and_1_out), .Q(d_ff_6_q));  // open: Qn, preset, en, reset
  D_Flip_Flop d_ff_7 (.clk(clock_7_out), .D(d_ff_6_q), .Q(d_ff_7_q));  // open: Qn, preset, en, reset
  D_Flip_Flop d_ff_8 (.clk(clock_2_out), .D(d_ff_1_q), .Q(d_ff_8_q[0]));  // open: Qn, preset, en, reset
  D_Flip_Flop d_ff_9 (.clk(clock_3_out), .D(d_ff_2_q), .Q(d_ff_8_q[1]));  // open: Qn, preset, en, reset
  D_Flip_Flop d_ff_10 (.clk(clock_4_out), .D(d_ff_3_q), .Q(d_ff_8_q[2]));  // open: Qn, preset, en, reset
  D_Flip_Flop d_ff_11 (.clk(clock_5_out), .D(d_ff_4_q), .Q(d_ff_8_q[3]));  // open: Qn, preset, en, reset
  D_Flip_Flop d_ff_12 (.clk(clock_6_out), .D(d_ff_5_q), .Q(d_ff_12_q));  // open: Qn, preset, en, reset
  D_Flip_Flop d_ff_13 (.clk(clock_7_out), .D(d_ff_7_q), .Q(d_ff_13_q));  // open: Qn, preset, en, reset
  and and_7 (and_7_out, d_ff_8_q[0], ~d_ff_6_q);  // AND_Gate
  and and_8 (and_8_out, d_ff_8_q[1], ~d_ff_7_q);  // AND_Gate
  and and_9 (and_9_out, d_ff_8_q[2], ~d_ff_13_q);  // AND_Gate
  and and_10 (and_10_out, d_ff_8_q[3], ~d_ff_14_q);  // AND_Gate
  and and_11 (and_11_out, d_ff_12_q, ~d_ff_15_q);  // AND_Gate
  D_Flip_Flop d_ff_14 (.clk(clock_7_out), .D(d_ff_13_q), .Q(d_ff_14_q));  // open: Qn, preset, en, reset
  D_Flip_Flop d_ff_15 (.clk(clock_7_out), .D(d_ff_14_q), .Q(d_ff_15_q));  // open: Qn, preset, en, reset
  // Probe on {{6{1'b0}}, d_ff_8_q}
  ROM #(.addrWidth(10), .dataWidth(7)) rom_2 (.addr({{6{1'b0}}, d_ff_8_q}), .data(rom_2_data));  // open: sel
  _7_Segment_Display u_7_segment_display_1 (
    .g(rom_2_data[5]), .f(rom_2_data[1]), .a(rom_2_data[0]), .b(rom_2_data[6]), .e(rom_2_data[2]),
    .d(rom_2_data[3]), .c(rom_2_data[4]));  // open: dp

  // Notes on the sheet:
  //   contents of rom_1 (hex, n*v repeats v):
  //   6*0 1 4*0 2 2 2 9*0 4*2
  //   contents of rom_2 (hex, n*v repeats v):
  //   0 5f 50 11 6d 22 44 44 79 55 66 77
endmodule
