// Logisim project rom.circ as structural Verilog: 1 circuit, main circuit main
module main (
);

  wire and_1_out, and_2_out, and_3_out, and_4_out, and_5_out, and_6_out, and_7_out, and_8_out, and_9_out,
       and_10_out, and_11_out, and_12_out, and_13_out, and_14_out, and_15_out, and_16_out, and_17_out,
       and_18_out, and_19_out, and_20_out, and_21_out, and_22_out, and_23_out, and_24_out, and_25_out,
       and_26_out, and_27_out, and_28_out, and_29_out, and_30_out, and_31_out, and_32_out, and_33_out,
       and_34_out, and_35_out, and_36_out, and_37_out, and_38_out, and_39_out, and_40_out, and_41_out,
       and_42_out, and_43_out, and_44_out, and_45_out, and_46_out, and_47_out, and_48_out, and_49_out,
       and_50_out, and_51_out, and_52_out, and_53_out, and_54_out, and_55_out, and_56_out, and_57_out,
       and_58_out, and_59_out, and_60_out, and_61_out, and_62_out, and_63_out, and_64_out, and_65_out,
       clock_1_out, clock_2_out, counter_1_carry, d_ff_1_q, d_ff_2_q, d_ff_3_q, d_ff_4_q, d_ff_5_q, d_ff_6_q,
       d_ff_7_q, d_ff_8_q, or_1_out, or_2_out, or_3_out, or_4_out, or_5_out, or_6_out, or_7_out, or_8_out,
       or_9_out, or_10_out, or_11_out, or_12_out, or_13_out, or_14_out, or_15_out, or_16_out, or_17_out,
       or_18_out, or_19_out, or_20_out, or_21_out, or_22_out, or_23_out, or_24_out, or_25_out, or_26_out,
       or_27_out, or_28_out, or_29_out, or_30_out, or_31_out, or_32_out, or_33_out;

  Clock clock_1 (.out(clock_1_out));
  Counter #(.width(4), .max('hf)) counter_1 (
    .load(1'b0), .D(4'b1111), .count(1'b1), .carry(counter_1_carry), .clk(clock_1_out), .clr(1'b0));  // open: Q
  Clock clock_2 (.out(clock_2_out));
  D_Flip_Flop d_ff_1 (.clk(clock_2_out), .D(counter_1_carry), .Q(d_ff_1_q));  // open: Qn, preset, en, reset
  and and_1 (and_1_out, ~1'b0, and_2_out);  // AND_Gate
  or or_1 (or_1_out, 1'b0, and_2_out);
  and and_2 (and_2_out, ~1'b0, and_3_out);  // AND_Gate
  or or_2 (or_2_out, 1'b0, and_3_out);
  and and_3 (and_3_out, ~1'b0, and_4_out);  // AND_Gate
  or or_3 (or_3_out, 1'b0, and_4_out);
  and and_4 (and_4_out, ~1'b0, and_5_out);  // AND_Gate
  or or_4 (or_4_out, 1'b0, and_5_out);
  and and_5 (and_5_out, ~1'b0, and_6_out);  // AND_Gate
  or or_5 (or_5_out, 1'b0, and_6_out);
  and and_6 (and_6_out, ~1'b0, and_8_out);  // AND_Gate
  and and_7 (and_7_out, 1'b0, ~and_8_out);  // AND_Gate
  and and_8 (and_8_out, ~1'b0, d_ff_1_q);  // AND_Gate
  or or_6 (or_6_out, 1'b0, d_ff_1_q);
  D_Flip_Flop d_ff_2 (.clk(clock_2_out), .D(d_ff_1_q), .Q(d_ff_2_q));  // open: Qn, preset, en, reset
  and and_9 (and_9_out, ~or_1_out, and_11_out);  // AND_Gate
  and and_10 (and_10_out, or_1_out, ~and_11_out);  // AND_Gate
  and and_11 (and_11_out, ~or_2_out, and_13_out);  // AND_Gate
  and and_12 (and_12_out, or_2_out, ~and_13_out);  // AND_Gate
  and and_13 (and_13_out, ~or_3_out, and_15_out);  // AND_Gate
  and and_14 (and_14_out, or_3_out, ~and_15_out);  // AND_Gate
  and and_15 (and_15_out, ~or_4_out, and_17_out);  // AND_Gate
  and and_16 (and_16_out, or_4_out, ~and_17_out);  // AND_Gate
  and and_17 (and_17_out, ~or_5_out, and_18_out);  // AND_Gate
  or or_7 (or_7_out, or_5_out, and_18_out);
  and and_18 (and_18_out, ~and_7_out, and_20_out);  // AND_Gate
  and and_19 (and_19_out, and_7_out, ~and_20_out);  // AND_Gate
  and and_20 (and_20_out, ~or_6_out, d_ff_2_q);  // AND_Gate
  or or_8 (or_8_out, or_6_out, d_ff_2_q);
  D_Flip_Flop d_ff_3 (.clk(clock_2_out), .D(d_ff_2_q), .Q(d_ff_3_q));  // open: Qn, preset, en, reset
  D_Flip_Flop d_ff_4 (.clk(clock_2_out), .D(d_ff_3_q), .Q(d_ff_4_q));  // open: Qn, preset, en, reset
  and and_21 (and_21_out, ~and_10_out, and_22_out);  // AND_Gate
  or or_9 (or_9_out, and_10_out, and_22_out);
  and and_22 (and_22_out, ~and_12_out, and_24_out);  // AND_Gate
  and and_23 (and_23_out, and_12_out, ~and_24_out);  // AND_Gate
  and and_24 (and_24_out, ~and_14_out, and_25_out);  // AND_Gate
  or or_10 (or_10_out, and_14_out, and_25_out);
  and and_25 (and_25_out, ~and_16_out, and_26_out);  // AND_Gate
  or or_11 (or_11_out, and_16_out, and_26_out);
  and and_26 (and_26_out, ~or_7_out, and_28_out);  // AND_Gate
  and and_27 (and_27_out, or_7_out, ~and_28_out);  // AND_Gate
  and and_28 (and_28_out, ~and_19_out, and_29_out);  // AND_Gate
  or or_12 (or_12_out, and_19_out, and_29_out);
  and and_29 (and_29_out, ~or_8_out, d_ff_3_q);  // AND_Gate
  or or_13 (or_13_out, or_8_out, d_ff_3_q);
  and and_30 (and_30_out, ~or_9_out, and_31_out);  // AND_Gate
  or or_14 (or_14_out, or_9_out, and_31_out);
  and and_31 (and_31_out, ~and_23_out, and_33_out);  // AND_Gate
  and and_32 (and_32_out, and_23_out, ~and_33_out);  // AND_Gate
  and and_33 (and_33_out, ~or_10_out, and_35_out);  // AND_Gate
  and and_34 (and_34_out, or_10_out, ~and_35_out);  // AND_Gate
  and and_35 (and_35_out, ~or_11_out, and_36_out);  // AND_Gate
  or or_15 (or_15_out, or_11_out, and_36_out);
  and and_36 (and_36_out, ~and_27_out, and_37_out);  // AND_Gate
  or or_16 (or_16_out, and_27_out, and_37_out);
  and and_37 (and_37_out, ~or_12_out, and_38_out);  // AND_Gate
  or or_17 (or_17_out, or_12_out, and_38_out);
  and and_38 (and_38_out, ~or_13_out, d_ff_4_q);  // AND_Gate
  or or_18 (or_18_out, or_13_out, d_ff_4_q);
  D_Flip_Flop d_ff_5 (.clk(clock_2_out), .D(d_ff_4_q), .Q(d_ff_5_q));  // open: Qn, preset, en, reset
  and and_39 (and_39_out, ~or_14_out, and_41_out);  // AND_Gate
  and and_40 (and_40_out, or_14_out, ~and_41_out);  // AND_Gate
  and and_41 (and_41_out, ~and_32_out, and_42_out);  // AND_Gate
  or or_19 (or_19_out, and_32_out, and_42_out);
  and and_42 (and_42_out, ~and_34_out, and_44_out);  // AND_Gate
  and and_43 (and_43_out, and_34_out, ~and_44_out);  // AND_Gate
  and and_44 (and_44_out, ~or_15_out, and_46_out);  // AND_Gate
  and and_45 (and_45_out, or_15_out, ~and_46_out);  // AND_Gate
  and and_46 (and_46_out, ~or_16_out, and_47_out);  // AND_Gate
  or or_20 (or_20_out, or_16_out, and_47_out);
  and and_47 (and_47_out, ~or_17_out, and_48_out);  // AND_Gate
  or or_21 (or_21_out, or_17_out, and_48_out);
  and and_48 (and_48_out, ~or_18_out, d_ff_5_q);  // AND_Gate
  or or_22 (or_22_out, or_18_out, d_ff_5_q);
  D_Flip_Flop d_ff_6 (.clk(clock_2_out), .D(d_ff_5_q), .Q(d_ff_6_q));  // open: Qn, preset, en, reset
  and and_49 (and_49_out, ~and_40_out, and_50_out);  // AND_Gate
  or or_23 (or_23_out, and_40_out, and_50_out);
  and and_50 (and_50_out, ~or_19_out, and_51_out);  // AND_Gate
  or or_24 (or_24_out, or_19_out, and_51_out);
  and and_51 (and_51_out, ~and_43_out, and_53_out);  // AND_Gate
  and and_52 (and_52_out, and_43_out, ~and_53_out);  // AND_Gate
  and and_53 (and_53_out, ~and_45_out, and_54_out);  // AND_Gate
  or or_25 (or_25_out, and_45_out, and_54_out);
  and and_54 (and_54_out, ~or_20_out, and_55_out);  // AND_Gate
  or or_26 (or_26_out, or_20_out, and_55_out);
  and and_55 (and_55_out, ~or_21_out, and_56_out);  // AND_Gate
  or or_27 (or_27_out, or_21_out, and_56_out);
  and and_56 (and_56_out, ~or_22_out, d_ff_6_q);  // AND_Gate
  and and_57 (and_57_out, or_22_out, ~d_ff_6_q);  // AND_Gate
  D_Flip_Flop d_ff_7 (.clk(clock_2_out), .D(d_ff_6_q), .Q(d_ff_7_q));  // open: Qn, preset, en, reset
  D_Flip_Flop d_ff_8 (.clk(clock_2_out), .D(d_ff_7_q), .Q(d_ff_8_q));  // open: Qn, preset, en, reset
  and and_58 (and_58_out, ~or_23_out, and_59_out);  // AND_Gate
  or or_28 (or_28_out, or_23_out, and_59_out);
  and and_59 (and_59_out, ~or_24_out, and_60_out);  // AND_Gate
  or or_29 (or_29_out, or_24_out, and_60_out);
  and and_60 (and_60_out, ~and_52_out, and_61_out);  // AND_Gate
  or or_30 (or_30_out, and_52_out, and_61_out);
  and and_61 (and_61_out, ~or_25_out, and_62_out);  // AND_Gate
  or or_31 (or_31_out, or_25_out, and_62_out);
  and and_62 (and_62_out, ~or_26_out, and_63_out);  // AND_Gate
  or or_32 (or_32_out, or_26_out, and_63_out);
  and and_63 (and_63_out, ~or_27_out, and_64_out);  // AND_Gate
  or or_33 (or_33_out, or_27_out, and_64_out);
  and and_64 (and_64_out, ~and_57_out, d_ff_7_q);  // AND_Gate
  and and_65 (and_65_out, and_57_out, ~d_ff_7_q);  // AND_Gate
  _7_Segment_Display u_7_segment_display_1 (
    .g(or_33_out), .f(or_29_out), .a(or_28_out), .b(and_65_out), .e(or_30_out), .d(or_31_out), .c(or_32_out));  // open: dp
  D_Flip_Flop d_ff_9 (.clk(clock_2_out), .D(d_ff_8_q));  // open: Q, Qn, preset, en, reset
endmodule
